# Fritzing sketch Updated_Microscope_potentiometer (saved by Fritzing 0.9.3b)
breadboards: 1

parts:
  Power_plug2 = Power plug
  U1 = POT [package=pot_alpha_rv16af-20]
  S1 = TILT-SWITCH-SW-200D [package=reed_switch_plastic]
  LED1 = LEDs [package=led10mm]

nets:
  N1: Power_plug2.GND, U1.A, LED1.C, LED1.A
  N2: Power_plug2.VCC, S1.1
  N3: U1.S, S1.2
